# Fritzing sketch stripboard (saved by Fritzing 0.9.4)
stripboards: 1

parts:
  Part1 = Arduino Nano (Rev3.0)
  U1 = MIDI_CONN_FEMALE_SUPPORT [package=din_5_female_support]
  R1 = Resistor [tolerance=±5% resistance=220 package=THT]
  U2 = MIDI_CONN_FEMALE_SUPPORT [package=din_5_female_support]

nets:
  N1: Part1.GND, U1.NC1, U2.NC1
  N2: Part1.D2, U2.MIDI_IN
  N3: Part1.D3, U1.NC2
  N4: Part1.D4, U1.MIDI_IN
  N5: Part1.D9, U1.NC3
  N6: Part1.5V, U1.MIDI_OUT, R1.Pin_0
  N7: R1.Pin_1, U2.MIDI_OUT

notes:
  MIDI OUT
  HARP IN
  Q
  U
  M
  I
